// Logisim project sap1.circ as structural Verilog: 2 circuits, main circuit main
module _8_bit_register (
  input  in_1,
  input  in_2,
  input  in_3,
  input  in_4,
  input  in_5,
  input  in_6,
  input  in_7,
  input  in_8,
  input  in_9,
  input  in_10,
  input  in_11
);

  wire [7:0] register_1_q;

  Register #(.trigger("high")) register_1 (
    .D({in_8, in_7, in_6, in_5, in_4, in_3, in_2, in_1}), .en(in_9), .Q(register_1_q), .clk(in_10),
    .clr(in_11));
  LED led_1 (.in(register_1_q[0]));
  LED led_2 (.in(register_1_q[1]));
  LED led_3 (.in(register_1_q[2]));
  LED led_4 (.in(register_1_q[3]));
  LED led_5 (.in(register_1_q[4]));
  LED led_6 (.in(register_1_q[5]));
  LED led_7 (.in(register_1_q[6]));
  LED led_8 (.in(register_1_q[7]));
endmodule

module main (
  input  Run_Step,
  input  in_2,
  input  in_3,
  input  in_4,
  input  in_5,
  input  in_6,
  input  in_7,
  input  in_8,
  input  in_9,
  input  in_10,
  input  in_11,
  input  in_12,
  input  in_13,
  input  in_14,
  input  in_15,
  input  in_16,
  input  in_17,
  input  in_18,
  input  in_19,
  input  in_20,
  input  in_21,
  input  in_22,
  input  in_23,
  input  Value,
  input  in_25,
  input  in_26,
  input  in_27,
  input  in_28,
  input  in_29,
  input  in_30,
  input  in_31,
  input  in_32,
  input  in_33,
  input  in_34,
  input  in_35,
  input  in_36,
  input  in_37,
  input  in_38,
  input  in_39,
  input  in_40,
  input  in_41,
  input  in_42,
  input  in_43,
  input  in_44,
  input  in_45
);

  wire AI, AND, and_1_out, and_2_out, and_3_out, AO, BI, button_1_out, button_3_out, C, CE, CLK, clock_1_out,
       CO, controlled_buffer_25_out, EO, FI, HLT, II, INV, IO, J, JC, JLZ, JMP, JZ, LO, MI, not_1_out,
       not_2_out, not_3_out, not_4_out, not_5_out, not_6_out, OI, OR, or_1_out, RI, RO, RST, S, SU, TR, XOR,
       Z;
  wire [1:0] nor_1_out;
  wire [2:0] counter_1_q, register_6_q;
  wire [7:0] adder_1_out, BUS, controlled_inverter_1_out, counter_2_q, multiplexer_2_out, multiplexer_3_out,
       ram_1_data, register_1_q, register_2_q, register_3_q, register_4_q, register_5_q;
  wire [23:0] rom_1_data;
  wire [31:0] rom_2_data;

  assign HLT = in_2 ? in_4 : 1'bz;  // Controlled_Buffer controlled_buffer_1
  assign MI = in_2 ? in_14 : 1'bz;  // Controlled_Buffer controlled_buffer_2
  assign RI = in_2 ? in_15 : 1'bz;  // Controlled_Buffer controlled_buffer_3
  assign RO = in_2 ? in_16 : 1'bz;  // Controlled_Buffer controlled_buffer_4
  assign IO = in_2 ? in_17 : 1'bz;  // Controlled_Buffer controlled_buffer_5
  assign II = in_2 ? in_18 : 1'bz;  // Controlled_Buffer controlled_buffer_6
  assign AI = in_2 ? in_19 : 1'bz;  // Controlled_Buffer controlled_buffer_7
  assign AO = in_2 ? in_20 : 1'bz;  // Controlled_Buffer controlled_buffer_8
  assign LO = in_2 ? in_21 : 1'bz;  // Controlled_Buffer controlled_buffer_9
  assign SU = in_2 ? in_22 : 1'bz;  // Controlled_Buffer controlled_buffer_10
  assign BI = in_2 ? in_23 : 1'bz;  // Controlled_Buffer controlled_buffer_11
  assign OI = in_2 ? in_32 : 1'bz;  // Controlled_Buffer controlled_buffer_12
  assign CE = in_2 ? in_33 : 1'bz;  // Controlled_Buffer controlled_buffer_13
  assign CO = in_2 ? in_34 : 1'bz;  // Controlled_Buffer controlled_buffer_14
  assign J = in_2 ? in_35 : 1'bz;  // Controlled_Buffer controlled_buffer_15
  assign TR = in_2 ? in_36 : 1'bz;  // Controlled_Buffer controlled_buffer_16
  assign FI = in_2 ? in_37 : 1'bz;  // Controlled_Buffer controlled_buffer_17
  assign INV = in_2 ? in_38 : 1'bz;  // Controlled_Buffer controlled_buffer_18
  assign JLZ = in_2 ? in_39 : 1'bz;  // Controlled_Buffer controlled_buffer_19
  assign JZ = in_2 ? in_40 : 1'bz;  // Controlled_Buffer controlled_buffer_20
  assign JC = in_2 ? in_41 : 1'bz;  // Controlled_Buffer controlled_buffer_21
  assign AND = in_2 ? in_42 : 1'bz;  // Controlled_Buffer controlled_buffer_22
  assign OR = in_2 ? in_43 : 1'bz;  // Controlled_Buffer controlled_buffer_23
  assign XOR = in_2 ? in_44 : 1'bz;  // Controlled_Buffer controlled_buffer_24
  Clock clock_1 (.out(clock_1_out));
  Button button_1 (.out(button_1_out));
  LED led_1 (.in(counter_1_q[2]));
  not not_1 (not_1_out, HLT);
  Multiplexer multiplexer_1 (.in0(clock_1_out), .in1(button_1_out), .out(CLK), .sel(Run_Step), .en(not_1_out));
  Multiplexer #(.width(8)) multiplexer_2 (
    .in0(BUS), .in1({Value, in_25, in_26, in_27, in_28, in_29, in_30, in_31}), .out(multiplexer_2_out),
    .sel(not_2_out), .en(1'b1));
  not not_2 (not_2_out, in_13);
  LED led_2 (.in(counter_1_q[0]));
  LED led_3 (.in(counter_1_q[1]));
  Counter #(.width(3), .max('h7), .ongoal("continue"), .trigger("falling")) counter_1 (
    .count(1'b1), .Q(counter_1_q), .clk(CLK), .clr(or_1_out));  // open: load, D, carry
  or or_1 (or_1_out, RST, TR);
  LED #(.active("false")) led_4 (.in(in_13));
  LED led_5 (.in(in_13));
  Register register_1 (.D(BUS), .en(MI), .Q(register_1_q), .clk(CLK), .clr(RST));
  Register register_2 (.D(BUS), .en(II), .Q(register_2_q), .clk(CLK), .clr(RST));
  LED led_6 (.in(multiplexer_3_out[7]));
  Multiplexer #(.width(8)) multiplexer_3 (
    .in0({in_5, in_6, in_7, in_8, in_9, in_10, in_11, in_12}), .in1(register_1_q), .out(multiplexer_3_out),
    .sel(in_13), .en(1'b1));
  assign controlled_buffer_25_out = RI ? CLK : 1'bz;  // Controlled_Buffer controlled_buffer_25
  assign BUS = IO ? {4'b0000, register_2_q[3:0]} : 8'bz;  // Controlled_Buffer controlled_buffer_26
  Pull_Resistor pull_resistor_1 (.node(RST));
  Button button_2 (.out(RST));
  LED led_7 (.in(multiplexer_3_out[6]));
  LED led_8 (.in(multiplexer_3_out[5]));
  LED led_9 (.in(multiplexer_3_out[4]));
  LED led_10 (.in(multiplexer_3_out[3]));
  not not_3 (not_3_out, controlled_buffer_25_out);
  assign controlled_buffer_25_out = button_3_out ? 1'b1 : 1'bz;  // Controlled_Buffer controlled_buffer_27
  Pull_Resistor pull_resistor_2 (.node(controlled_buffer_25_out));
  LED led_11 (.in(ram_1_data[7]));
  LED led_12 (.in(ram_1_data[6]));
  LED led_13 (.in(ram_1_data[4]));
  LED led_14 (.in(ram_1_data[5]));
  LED led_15 (.in(register_2_q[6]));
  LED led_16 (.in(register_2_q[4]));
  LED led_17 (.in(register_2_q[5]));
  LED led_18 (.in(register_2_q[7]));
  LED led_19 (.in(multiplexer_3_out[1]));
  LED led_20 (.in(multiplexer_3_out[2]));
  LED led_21 (.in(multiplexer_3_out[0]));
  assign BUS = RO ? ram_1_data : 8'bz;  // Controlled_Buffer controlled_buffer_28
  RAM #(.bus("separate")) ram_1 (
    .addr(multiplexer_3_out), .din(multiplexer_2_out), .data(ram_1_data), .str(controlled_buffer_25_out),
    .sel(1'b1), .clk(controlled_buffer_25_out), .ld(not_3_out), .clr(1'b0));
  Button button_3 (.out(button_3_out));
  LED led_22 (.in(ram_1_data[2]));
  LED led_23 (.in(ram_1_data[0]));
  LED led_24 (.in(ram_1_data[1]));
  LED led_25 (.in(ram_1_data[3]));
  LED led_26 (.in(register_2_q[1]));
  LED led_27 (.in(register_2_q[0]));
  LED led_28 (.in(register_2_q[2]));
  LED led_29 (.in(register_2_q[3]));
  ROM #(.addrWidth(11), .dataWidth(24)) rom_1 (.addr({register_2_q, counter_1_q}), .data(rom_1_data), .sel(1'b1));
  LED led_30 (.in(BUS[7]));
  LED led_31 (.in(BUS[5]));
  LED led_32 (.in(BUS[6]));
  Pull_Resistor pull_resistor_3 (.node(BUS));
  assign BUS = in_3 ? {8{1'b1}} : 8'bz;  // Controlled_Buffer controlled_buffer_29
  not not_4 (not_4_out, in_2);
  assign {HLT, MI, RI, RO, IO, II, AI, AO, LO, SU, BI, OI, CE, CO, J, TR, FI, INV, JLZ, JZ, JC, AND, OR, XOR} = not_4_out ? rom_1_data : 24'bz;  // Controlled_Buffer controlled_buffer_30
  LED led_33 (.in(BUS[4]));
  LED led_34 (.in(BUS[1]));
  LED led_35 (.in(BUS[2]));
  LED led_36 (.in(BUS[3]));
  LED led_37 (.in(BUS[0]));
  LED led_38 (.in(HLT));
  Counter #(.ongoal("continue")) counter_2 (
    .load(JMP), .D(BUS), .count(CE), .Q(counter_2_q), .clk(CLK), .clr(RST));  // open: carry
  assign BUS = AO ? register_4_q : 8'bz;  // Controlled_Buffer controlled_buffer_31
  assign BUS = 1'b0 ? register_5_q : 8'bz;  // Controlled_Buffer controlled_buffer_32
  Register register_3 (.D(BUS), .en(OI), .Q(register_3_q), .clk(CLK), .clr(RST));
  LED led_39 (.in(MI));
  LED led_40 (.in(RI));
  LED led_41 (.in(IO));
  LED led_42 (.in(RO));
  LED led_43 (.in(counter_2_q[5]));
  LED led_44 (.in(counter_2_q[6]));
  LED led_45 (.in(counter_2_q[4]));
  LED led_46 (.in(counter_2_q[7]));
  assign BUS = CO ? counter_2_q : 8'bz;  // Controlled_Buffer controlled_buffer_33
  LED led_47 (.in(register_4_q[6]));
  LED led_48 (.in(register_4_q[7]));
  Register register_4 (.D(BUS), .en(AI), .Q(register_4_q), .clk(CLK), .clr(RST));
  assign controlled_inverter_1_out = SU ? ~register_5_q : 8'bz;  // Controlled_Inverter controlled_inverter_1
  not not_5 (not_5_out, SU);
  assign controlled_inverter_1_out = not_5_out ? register_5_q : 8'bz;  // Controlled_Buffer controlled_buffer_34
  LED led_49 (.in(register_5_q[6]));
  LED led_50 (.in(register_5_q[7]));
  Register register_5 (.D(BUS), .en(BI), .Q(register_5_q), .clk(CLK), .clr(RST));
  LED led_51 (.in(II));
  LED led_52 (.in(AI));
  LED led_53 (.in(EO));
  LED led_54 (.in(AO));
  LED led_55 (.in(counter_2_q[3]));
  LED led_56 (.in(counter_2_q[2]));
  LED led_57 (.in(counter_2_q[0]));
  LED led_58 (.in(counter_2_q[1]));
  or or_2 (JMP, and_1_out, and_2_out, and_3_out, J);
  LED led_59 (.in(register_4_q[2]));
  LED led_60 (.in(register_4_q[4]));
  LED led_61 (.in(register_4_q[5]));
  LED led_62 (.in(register_4_q[3]));
  Adder adder_1 (.a(register_4_q), .b(controlled_inverter_1_out), .out(adder_1_out), .cin(SU), .cout(nor_1_out[1]));
  LED led_63 (.in(register_5_q[4]));
  LED led_64 (.in(register_5_q[2]));
  LED led_65 (.in(register_5_q[3]));
  LED led_66 (.in(register_5_q[5]));
  ROM #(.addrWidth(9), .dataWidth(32)) rom_2 (.addr({in_45, register_3_q}), .data(rom_2_data), .sel(1'b1));
  LED led_67 (.in(BI));
  LED led_68 (.in(SU));
  LED led_69 (.in(OI));
  LED led_70 (.in(CE));
  LED led_71 (.in(register_4_q[0]));
  LED led_72 (.in(register_4_q[1]));
  LED led_73 (.in(adder_1_out[6]));
  LED led_74 (.in(adder_1_out[5]));
  LED led_75 (.in(adder_1_out[7]));
  LED led_76 (.in(adder_1_out[4]));
  assign BUS = LO ? adder_1_out : 8'bz;  // Controlled_Buffer controlled_buffer_35
  LED led_77 (.in(register_5_q[0]));
  LED led_78 (.in(register_5_q[1]));
  LED led_79 (.in(J));
  LED led_80 (.in(TR));
  LED led_81 (.in(FI));
  LED led_82 (.in(CO));
  and and_1 (and_1_out, S, JLZ);
  and and_2 (and_2_out, C, JC);
  and and_3 (and_3_out, Z, JZ);
  nor nor_1 (nor_1_out[0], register_4_q[0], register_4_q[1], register_4_q[2], register_4_q[3], register_4_q[4], register_4_q[5], register_4_q[6], register_4_q[7]);
  LED led_83 (.in(adder_1_out[3]));
  LED led_84 (.in(adder_1_out[1]));
  LED led_85 (.in(adder_1_out[2]));
  LED led_86 (.in(adder_1_out[0]));
  _7_Segment_Display u_7_segment_display_1 (
    .g(rom_2_data[27]), .f(rom_2_data[26]), .a(rom_2_data[25]), .b(rom_2_data[24]), .e(rom_2_data[31]),
    .d(rom_2_data[30]), .c(rom_2_data[29]), .dp(rom_2_data[28]));
  _7_Segment_Display u_7_segment_display_2 (
    .g(rom_2_data[19]), .f(rom_2_data[18]), .a(rom_2_data[17]), .b(rom_2_data[16]), .e(rom_2_data[23]),
    .d(rom_2_data[22]), .c(rom_2_data[21]), .dp(rom_2_data[20]));
  LED led_87 (.in(JLZ));
  LED led_88 (.in(JZ));
  LED led_89 (.in(JC));
  LED led_90 (.in(INV));
  assign {S, C, Z} = not_6_out ? register_6_q : 3'bz;  // Controlled_Buffer controlled_buffer_36
  Register #(.width(3), .trigger("falling")) register_6 (
    .D({register_4_q[7], nor_1_out}), .en(FI), .Q(register_6_q), .clk(CLK));  // open: clr
  assign {S, C, Z} = INV ? ~register_6_q : 3'bz;  // Controlled_Inverter controlled_inverter_2
  _7_Segment_Display u_7_segment_display_3 (
    .g(rom_2_data[11]), .f(rom_2_data[10]), .a(rom_2_data[9]), .b(rom_2_data[8]), .e(rom_2_data[15]),
    .d(rom_2_data[14]), .c(rom_2_data[13]), .dp(rom_2_data[12]));
  _7_Segment_Display u_7_segment_display_4 (
    .g(rom_2_data[3]), .f(rom_2_data[2]), .a(rom_2_data[1]), .b(rom_2_data[0]), .e(rom_2_data[7]),
    .d(rom_2_data[6]), .c(rom_2_data[5]), .dp(rom_2_data[4]));
  LED led_91 (.in(XOR));
  LED led_92 (.in(AND));
  LED led_93 (.in(OR));
  LED led_94 (.in(C));
  LED led_95 (.in(S));
  not not_6 (not_6_out, INV);
  LED led_96 (.in(Z));

  // Other names for the same wires on the sheet: MANUAL = in_2; PRGM_RUN = in_13

  // Notes on the sheet:
  //   Step
  //   Instruction Register
  //   Microcode Counter
  //   RAM Contents
  //   Instruction ROM
  //   LOAD
  //   contents of rom_1 (hex, n*v repeats v):
  //   400400 140800 6*0 400400 140800 400400 500000 120800 100 0 0 400400 140800 400400 500000 102000
  //   28800 100 0 400400 140800 400400 500000 102000 2c800 100 0 400400 140800 400400 500000 0 120800 100
  //   0 400400 140800 6*0 400400 140800 400400 100a00 100 0 0 0 400400 140800 80080 5*0 400400 140800 6*0
  //   400400 140800 6*0 400400 140800 6*0 400400 140800 6*0 400400 140800 6*0 400400 140800 6*0 400400
  //   140800 6*0 400400 140800 6*0 400400 140800 6*0 400400 140800 6*0 400400 140800 6*0 400400 140800 6*0
  //   400400 140800 6*0 400400 140800 6*0 400400 140800 6*0 400400 140800 6*0 400400 140800 6*0 400400
  //   140800 6*0 400400 140800 6*0 400400 140800 6*0 400400 140800 6*0 400400 140800 6*0 400400 140800 6*0
  //   400400 140800 6*0 400400 140800 480000 102000 28000 100 0 0 400400 140800 480000 102000 28000 100 0
  //   0 400400 140800 480000 102000 28000 100 0 0 400400 140800 480000 102000 28000 100 0 0 400400 140800
  //   480000 102000 28000 100 0 0 400400 140800 480000 102000 28000 100 0 0 400400 140800 480000 102000
  //   28000 100 0 0 400400 140800 480000 102000 28000 100 0 0 400400 140800 480000 102000 28000 100 0 0
  //   400400 140800 480000 102000 28000 100 0 0 400400 140800 480000 102000 28000 100 0 0 400400 140800
  //   480000 102000 28000 100 0 0 400400 140800 480000 102000 28000 100 0 0 400400 140800 480000 102000
  //   28000 100 0 0 400400 140800 480000 102000 28000 100 0 0 400400 140800 480000 102000 28000 100 0 0
  //   400400 140800 480000 102000 2c000 100 0 0 400400 140800 480000 102000 2c000 100 0 0 400400 140800
  //   480000 102000 2c000 100 0 0 400400 140800 480000 102000 2c000 100 0 0 400400 140800 480000 102000
  //   2c000 100 0 0 400400 140800 480000 102000 2c000 100 0 0 400400 140800 480000 102000 2c000 100 0 0
  //   400400 140800 480000 102000 2c000 100 0 0 400400 140800 480000 102000 2c000 100 0 0 400400 140800
  //   480000 102000 2c000 100 0 0 400400 140800 480000 102000 2c000 100 0 0 400400 140800 480000 102000
  //   2c000 100 0 0 400400 140800 480000 102000 2c000 100 0 0 400400 140800 480000 102000 2c000 100 0 0
  //   400400 140800 480000 102000 2c000 100 0 0 400400 140800 480000 102000 2c000 100 0 0 400400 140800
  //   480000 210000 100 0 0 0 400400 140800 480000 210000 100 0 0 0 400400 140800 480000 210000 100 0 0 0
  //   400400 140800 480000 210000 100 0 0 0 400400 140800 480000 210000 100 0 0 0 400400 140800 480000
  //   210000 100 0 0 0 400400 140800 480000 210000 100 0 0 0 400400 140800 480000 210000 100 0 0 0 400400
  //   140800 480000 210000 100 0 0 0 400400 140800 480000 210000 100 0 0 0 400400 140800 480000 210000 100
  //   0 0 0 400400 140800 480000 210000 100 0 0 0 400400 140800 480000 210000 100 0 0 0 400400 140800
  //   480000 210000 100 0 0 0 400400 140800 480000 210000 100 0 0 0 400400 140800 480000 210000 100 0 0 0
  //   400400 140800 a0000 100 4*0 400400 140800 a0000 100 4*0 400400 140800 a0000 100 4*0 400400 140800
  //   a0000 100 4*0 400400 140800 a0000 100 4*0 400400 140800 a0000 100 4*0 400400 140800 a0000 100 4*0
  //   400400 140800 a0000 100 4*0 400400 140800 a0000 100 4*0 400400 140800 a0000 100 4*0 400400 140800
  //   a0000 100 4*0 400400 140800 a0000 100 4*0 400400 140800 a0000 100 4*0 400400 140800 a0000 100 4*0
  //   400400 140800 a0000 100 4*0 400400 140800 a0000 100 4*0 400400 140800 80200 100 4*0 400400 140800
  //   80200 100 4*0 400400 140800 80200 100 4*0 400400 140800 80200 100 4*0 400400 140800 80200 100 4*0
  //   400400 140800 80200 100 4*0 400400 140800 80200 100 4*0 400400 140800 80200 100 4*0 400400 140800
  //   80200 100 4*0 400400 140800 80200 100 4*0 400400 140800 80200 100 4*0 400400 140800 80200 100 4*0
  //   400400 140800 80200 100 4*0 400400 140800 80200 100 4*0 400400 140800 80200 100 4*0 400400 140800
  //   80200 100 4*0 400400 140800 6*0 400400 140800 6*0 400400 140800 6*0 400400 140800 6*0 400400 140800
  //   6*0 400400 140800 6*0 400400 140800 6*0 400400 140800 6*0 400400 140800 6*0 400400 140800 6*0 400400
  //   140800 6*0 400400 140800 6*0 400400 140800 6*0 400400 140800 6*0 400400 140800 6*0 400400 140800 6*0
  //   400400 140800 6*0 400400 140800 6*0 400400 140800 6*0 400400 140800 6*0 400400 140800 6*0 400400
  //   140800 6*0 400400 140800 6*0 400400 140800 6*0 400400 140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
  //   A Register
  //   Output Register
  //   Control Word
  //   Program Counter
  //   ALU
  //   B Register
  //   Output ROM
  //   contents of rom_2 (hex, n*v repeats v):
  //   e7 21 cb 6b 2d 6e ee 23 ef 6f 21e7 2121 21cb 216b 212d 216e 21ee 2123 21ef 216f cbe7 cb21 cbcb cb6b
  //   cb2d cb6e cbee cb23 cbef cb6f 6be7 6b21 6bcb 6b6b 6b2d 6b6e 6bee 6b23 6bef 6b6f 2de7 2d21 2dcb 2d6b
  //   2d2d 2d6e 2dee 2d23 2def 2d6f 6ee7 6e21 6ecb 6e6b 6e2d 6e6e 6eee 6e23 6eef 6e6f eee7 ee21 eecb ee6b
  //   ee2d ee6e eeee ee23 eeef ee6f 23e7 2321 23cb 236b 232d 236e 23ee 2323 23ef 236f efe7 ef21 efcb ef6b
  //   ef2d ef6e efee ef23 efef ef6f 6fe7 6f21 6fcb 6f6b 6f2d 6f6e 6fee 6f23 6fef 6f6f 21e7e7 21e721 21e7cb
  //   21e76b 21e72d 21e76e 21e7ee 21e723 21e7ef 21e76f 2121e7 212121 2121cb 21216b 21212d 21216e 2121ee
  //   212123 2121ef 21216f 21cbe7 21cb21 21cbcb 21cb6b 21cb2d 21cb6e 21cbee 21cb23 21cbef 21cb6f 216be7
  //   216b21 216bcb 216b6b 216b2d 216b6e 216bee 216b23 216bef 216b6f 212de7 212d21 212dcb 212d6b 212d2d
  //   212d6e 212dee 212d23 212def 212d6f 216ee7 216e21 216ecb 216e6b 216e2d 216e6e 216eee 216e23 216eef
  //   216e6f 21eee7 21ee21 21eecb 21ee6b 21ee2d 21ee6e 21eeee 21ee23 21eeef 21ee6f 2123e7 212321 2123cb
  //   21236b 21232d 21236e 2123ee 212323 2123ef 21236f 21efe7 21ef21 21efcb 21ef6b 21ef2d 21ef6e 21efee
  //   21ef23 21efef 21ef6f 216fe7 216f21 216fcb 216f6b 216f2d 216f6e 216fee 216f23 216fef 216f6f cbe7e7
  //   cbe721 cbe7cb cbe76b cbe72d cbe76e cbe7ee cbe723 cbe7ef cbe76f cb21e7 cb2121 cb21cb cb216b cb212d
  //   cb216e cb21ee cb2123 cb21ef cb216f cbcbe7 cbcb21 cbcbcb cbcb6b cbcb2d cbcb6e cbcbee cbcb23 cbcbef
  //   cbcb6f cb6be7 cb6b21 cb6bcb cb6b6b cb6b2d cb6b6e cb6bee cb6b23 cb6bef cb6b6f cb2de7 cb2d21 cb2dcb
  //   cb2d6b cb2d2d cb2d6e cb2dee cb2d23 cb2def cb2d6f cb6ee7 cb6e21 cb6ecb cb6e6b cb6e2d cb6e6e e7 21 cb
  //   6b 2d 6e ee 23 ef 6f 21e7 2121 21cb 216b 212d 216e 21ee 2123 21ef 216f cbe7 cb21 cbcb cb6b cb2d cb6e
  //   cbee cb23 cbef cb6f 6be7 6b21 6bcb 6b6b 6b2d 6b6e 6bee 6b23 6bef 6b6f 2de7 2d21 2dcb 2d6b 2d2d 2d6e
  //   2dee 2d23 2def 2d6f 6ee7 6e21 6ecb 6e6b 6e2d 6e6e 6eee 6e23 6eef 6e6f eee7 ee21 eecb ee6b ee2d ee6e
  //   eeee ee23 eeef ee6f 23e7 2321 23cb 236b 232d 236e 23ee 2323 23ef 236f efe7 ef21 efcb ef6b ef2d ef6e
  //   efee ef23 efef ef6f 6fe7 6f21 6fcb 6f6b 6f2d 6f6e 6fee 6f23 6fef 6f6f 21e7e7 21e721 21e7cb 21e76b
  //   21e72d 21e76e 21e7ee 21e723 21e7ef 21e76f 2121e7 212121 2121cb 21216b 21212d 21216e 2121ee 212123
  //   2121ef 21216f 21cbe7 21cb21 21cbcb 21cb6b 21cb2d 21cb6e 21cbee 21cb23 821cbef 821cb23 821cbee
  //   821cb6e 821cb2d 821cb6b 821cbcb 821cb21 821cbe7 821216f 82121ef 8212123 82121ee 821216e 821212d
  //   821216b 82121cb 8212121 82121e7 821e76f 821e7ef 821e723 821e7ee 821e76e 821e72d 821e76b 821e7cb
  //   821e721 821e7e7 8006f6f 8006fef 8006f23 8006fee 8006f6e 8006f2d 8006f6b 8006fcb 8006f21 8006fe7
  //   800ef6f 800efef 800ef23 800efee 800ef6e 800ef2d 800ef6b 800efcb 800ef21 800efe7 800236f 80023ef
  //   8002323 80023ee 800236e 800232d 800236b 80023cb 8002321 80023e7 800ee6f 800eeef 800ee23 800eeee
  //   800ee6e 800ee2d 800ee6b 800eecb 800ee21 800eee7 8006e6f 8006eef 8006e23 8006eee 8006e6e 8006e2d
  //   8006e6b 8006ecb 8006e21 8006ee7 8002d6f 8002def 8002d23 8002dee 8002d6e 8002d2d 8002d6b 8002dcb
  //   8002d21 8002de7 8006b6f 8006bef 8006b23 8006bee 8006b6e 8006b2d 8006b6b 8006bcb 8006b21 8006be7
  //   800cb6f 800cbef 800cb23 800cbee 800cb6e 800cb2d 800cb6b 800cbcb 800cb21 800cbe7 800216f 80021ef
  //   8002123 80021ee 800216e 800212d 800216b 80021cb 8002121 80021e7 800006f 80000ef 8000023 80000ee
  //   800006e 800002d 800006b 80000cb 8000021
  //   C
  //   S
  //   Z
endmodule
